# Fritzing sketch MagLock Diagram (saved by Fritzing 0.9.3b)
breadboards: 1

parts:
  Raspberry_Pi_1 = Raspberry Pi 3 [part_number=RPI-3-V1.2]
  R1 = Resistor [tolerance=±5% resistance=1k package=THT]
  L1 = Solenoid
  D1 = Schottky Diode [part_number=1N5817 package="300 mil [THT]"]
  Q1 = NPN-Transistor [package="TO92 [THT]"]

nets:
  GND: Raspberry_Pi_1.GND, Q1.E
  N1: Raspberry_Pi_1.GIPO16, R1.Pin_0
  5V: Raspberry_Pi_1.5V
  N2: R1.Pin_1, Q1.B
  10V: L1.pin1, D1.cathode
  N3: L1.pin2, D1.anode, Q1.C

notes:
  Magnetic Lock Solenoid Raspberry Pi3
